// Logisim project C_1_9.circ as structural Verilog: 2 circuits, main circuit main
module main (
  input  [1:0] R2,
  input  [1:0] R1,
  input  [1:0] address_of_the_register,
  input  [3:0] data,
  input  in_5,
  input  read_write,
  input  [3:0] in_7,
  input  in_8,
  input  in_9,
  input  [3:0] in_10,
  input  in_11,
  input  in_12,
  input  [3:0] in_13,
  input  in_14,
  input  in_15,
  input  in_16
);

  wire clock_1_out, not_1_out;
  wire [3:0] adder_1_out, controlled_buffer_1_out, multiplexer_1_out, multiplexer_2_out, multiplexer_3_out,
       multiplexer_4_out, multiplexer_5_out, multiplexer_6_out, n4_bit_register_file_1_read_data_1,
       n4_bit_register_file_1_read_data_2, RA_q, RB_q, register_1_q, register_2_q, RM_q, xor_1_out;

  Multiplexer #(.width(4), .enable("false")) multiplexer_1 (
    .in0(data), .in1(register_2_q), .out(multiplexer_1_out), .sel(in_5));
  Clock clock_1 (.out(clock_1_out));
  Adder #(.width(4)) adder_1 (.a(RA_q), .b(multiplexer_2_out), .out(adder_1_out));  // open: cin, cout
  _4_bit_register_file u_4_bit_register_file_1 (
    .read_register_1(R2), .read_register_2(R1), .write_register(address_of_the_register),
    .write_data(multiplexer_1_out), .read_data_1(n4_bit_register_file_1_read_data_1),
    .read_data_2(n4_bit_register_file_1_read_data_2), .register_write(read_write), .clock(clock_1_out));
  Register #(.width(4)) RA (.D(n4_bit_register_file_1_read_data_2), .Q(RA_q), .clk(clock_1_out));  // open: en, clr
  Register #(.width(4)) RB (.D(n4_bit_register_file_1_read_data_1), .Q(RB_q), .clk(clock_1_out));  // open: en, clr
  Multiplexer #(.width(4), .enable("false")) multiplexer_2 (
    .in0(RB_q), .in1(in_7), .out(multiplexer_2_out), .sel(in_8));
  assign xor_1_out = multiplexer_2_out ^ RA_q;  // XOR_Gate xor_1, 4 bits wide
  Register #(.width(4)) RM (.D(RB_q), .Q(RM_q), .clk(clock_1_out));  // open: en, clr
  Register #(.width(4)) register_1 (.D(multiplexer_6_out), .Q(register_1_q), .clk(clock_1_out));  // open: en, clr
  Multiplexer #(.width(4), .enable("false")) multiplexer_3 (
    .in0(register_1_q), .in1(controlled_buffer_1_out), .out(multiplexer_3_out), .sel(in_16));
  Multiplexer #(.width(4), .enable("false")) multiplexer_4 (
    .in0(RM_q), .in1(in_10), .out(multiplexer_4_out), .sel(in_11));
  Multiplexer #(.width(4), .enable("false")) multiplexer_5 (
    .in0(in_13), .in1(register_1_q), .out(multiplexer_5_out), .sel(in_14));
  Register #(.width(4)) register_2 (.D(multiplexer_3_out), .Q(register_2_q), .clk(clock_1_out));  // open: en, clr
  assign controlled_buffer_1_out = in_12 ? multiplexer_4_out : 4'bz;  // Controlled_Buffer controlled_buffer_1
  not not_1 (not_1_out, in_12);
  Multiplexer #(.width(4), .enable("false")) multiplexer_6 (
    .in0(adder_1_out), .in1(xor_1_out), .out(multiplexer_6_out), .sel(in_9));
  RAM #(.addrWidth(4), .dataWidth(4)) ram_1 (
    .addr(multiplexer_5_out), .data(controlled_buffer_1_out), .clk(clock_1_out), .ld(not_1_out), .clr(in_15));  // open: sel

  // Notes on the sheet:
  //   ADDER
  //   XOR
  //   RZ
  //   RY
  //   MAIN MEMORY
endmodule

module _4_bit_register_file (
  input  [1:0] read_register_1,
  input  [1:0] read_register_2,
  input  register_write,
  input  [1:0] write_register,
  input  [3:0] write_data,
  input  clock,
  output [3:0] read_data_1,
  output [3:0] read_data_2
);

  wire and_1_out, and_2_out, and_3_out, and_4_out, decoder_1_out0, decoder_1_out1, decoder_1_out2,
       decoder_1_out3;
  wire [3:0] register_1_q, register_2_q, register_4_q;

  Decoder #(.select(2)) decoder_1 (
    .out0(decoder_1_out0), .out1(decoder_1_out1), .out2(decoder_1_out2), .out3(decoder_1_out3),
    .sel(write_register));  // open: en
  and and_1 (and_1_out, decoder_1_out0, register_write);
  and and_2 (and_2_out, decoder_1_out1, register_write);
  Register #(.width(4)) register_1 (.D(write_data), .en(and_1_out), .Q(register_1_q), .clk(clock));  // open: clr
  Register #(.width(4)) register_2 (.D(write_data), .en(and_2_out), .Q(register_2_q), .clk(clock));  // open: clr
  and and_3 (and_3_out, decoder_1_out2, register_write);
  and and_4 (and_4_out, decoder_1_out3, register_write);
  Register #(.width(4)) register_3 (.D(write_data), .en(and_3_out), .Q(register_2_q), .clk(clock));  // open: clr
  Register #(.width(4)) register_4 (.D(write_data), .en(and_4_out), .Q(register_4_q), .clk(clock));  // open: clr
  Multiplexer #(.select(2), .width(4)) multiplexer_1 (
    .in0(register_1_q), .in1(register_2_q), .in2(register_2_q), .in3(register_4_q), .out(read_data_1),
    .sel(read_register_1));  // open: en
  Multiplexer #(.select(2), .width(4)) multiplexer_2 (
    .in0(register_1_q), .in1(register_2_q), .in2(register_2_q), .in3(register_4_q), .out(read_data_2),
    .sel(read_register_2));  // open: en
endmodule
